// Logisim project su.circ as structural Verilog
module CU (
  input  RstClk,
  input  RUN,
  output [2:0] T,
  output ClkOvr
);

  wire and_1_out, clock_1_out, State_carry;
  wire [1:0] State_q;

  Clock clock_1 (.out(clock_1_out));
  and and_1 (and_1_out, clock_1_out, RUN);
  Counter #(.max('h2), .width(2)) State (
    .clr(RstClk), .load(1'b0), .up(1'b1), .count(1'b1), .clk(and_1_out), .D(2'b00), .carry(State_carry),
    .Q(State_q));
  // NoConnect on State_carry
  Decoder #(.enable("false"), .select(2)) decoder_1 (
    .out0(T[0]), .out1(T[1]), .out2(T[2]), .out3(ClkOvr), .sel(State_q));
endmodule
